// Logisim project ti74138.circ as structural Verilog: 1 circuit, main circuit main
module main (
  input  in_1,
  input  in_2,
  input  in_3,
  input  in_4,
  input  in_5,
  input  in_6,
  output out_7,
  output out_8,
  output out_9,
  output out_10,
  output out_11,
  output out_12,
  output out_13,
  output out_14
);

  wire and_1_out, decoder_1_out0, decoder_1_out1, decoder_1_out2, decoder_1_out3, decoder_1_out4,
       decoder_1_out5, decoder_1_out6, decoder_1_out7;

  and and_1 (and_1_out, ~in_1, ~in_2, in_3);  // AND_Gate
  Decoder #(.select(3), .disabled(0), .enable("false")) decoder_1 (
    .out0(decoder_1_out0), .out1(decoder_1_out1), .out2(decoder_1_out2), .out3(decoder_1_out3),
    .out4(decoder_1_out4), .out5(decoder_1_out5), .out6(decoder_1_out6), .out7(decoder_1_out7),
    .sel({in_6, in_5, in_4}));
  nand nand_1 (out_7, and_1_out, decoder_1_out0);
  nand nand_2 (out_8, and_1_out, decoder_1_out1);
  nand nand_3 (out_9, and_1_out, decoder_1_out2);
  nand nand_4 (out_10, and_1_out, decoder_1_out3);
  nand nand_5 (out_11, and_1_out, decoder_1_out4);
  nand nand_6 (out_12, and_1_out, decoder_1_out5);
  nand nand_7 (out_13, and_1_out, decoder_1_out6);
  nand nand_8 (out_14, and_1_out, decoder_1_out7);
endmodule
