// Logisim project ti74181.circ as structural Verilog: 1 circuit, main circuit main
module main (
  input  c0,
  input  m,
  input  a0,
  input  b0,
  input  a1,
  input  b1,
  input  a2,
  input  b2,
  input  a3,
  input  b3,
  input  S0,
  input  S1,
  input  S2,
  input  S3,
  output f0,
  output f1,
  output a_b,
  output f2,
  output f3,
  output p,
  output c4,
  output g
);

  wire and_1_out, and_2_out, and_3_out, and_4_out, and_5_out, and_6_out, and_7_out, and_8_out, and_9_out,
       and_10_out, and_11_out, and_13_out, and_14_out, and_15_out, and_16_out, and_17_out, and_18_out,
       and_19_out, and_20_out, and_21_out, and_22_out, and_23_out, and_24_out, and_25_out, and_26_out,
       and_27_out, and_28_out, and_29_out, and_30_out, and_31_out, and_32_out, and_33_out, nand_1_out,
       nand_3_out, nor_1_out, nor_2_out, nor_3_out, nor_4_out, nor_5_out, nor_6_out, nor_7_out, nor_8_out,
       nor_9_out, nor_10_out, nor_11_out;

  nand nand_1 (nand_1_out, c0, m);
  and and_1 (and_1_out, m, nor_1_out);
  and and_2 (and_2_out, ~nor_1_out, nor_3_out);  // AND_Gate
  xor xor_1 (f0, nand_1_out, and_2_out);
  and and_3 (and_3_out, S1, ~b0);  // AND_Gate
  and and_4 (and_4_out, b0, S0);
  nor nor_1 (nor_1_out, a0, and_4_out, and_3_out);
  and and_5 (and_5_out, m, nor_3_out, c0);
  and and_6 (and_6_out, ~nor_4_out, nor_6_out);  // AND_Gate
  nor nor_2 (nor_2_out, and_1_out, and_5_out);
  xor xor_2 (f1, nor_2_out, and_6_out);
  and and_7 (and_7_out, ~b0, S2, a0);  // AND_Gate
  and and_8 (and_8_out, a0, b0, S3);
  nor nor_3 (nor_3_out, and_7_out, and_8_out);
  and and_9 (and_9_out, b1, S0);
  nor nor_4 (nor_4_out, a1, and_9_out, and_13_out);
  and and_10 (and_10_out, m, nor_1_out, nor_6_out);
  and and_11 (and_11_out, m, nor_4_out);
  and and_12 (a_b, f0, f1, f2, f3);
  and and_13 (and_13_out, S1, ~b1);  // AND_Gate
  and and_14 (and_14_out, m, c0, nor_3_out, nor_6_out);
  nor nor_5 (nor_5_out, and_11_out, and_10_out, and_14_out);
  xor xor_3 (f2, nor_5_out, and_17_out);
  and and_15 (and_15_out, ~b1, S2, a1);  // AND_Gate
  and and_16 (and_16_out, a1, S3, b1);
  nor nor_6 (nor_6_out, and_15_out, and_16_out);
  and and_17 (and_17_out, ~nor_7_out, nor_9_out);  // AND_Gate
  and and_18 (and_18_out, b2, S0);
  nor nor_7 (nor_7_out, a2, and_18_out, and_21_out);
  and and_19 (and_19_out, m, nor_4_out, nor_9_out);
  and and_20 (and_20_out, m, nor_7_out);
  and and_21 (and_21_out, S1, ~b2);  // AND_Gate
  and and_22 (and_22_out, ~b2, S2, a2);  // AND_Gate
  and and_23 (and_23_out, m, nor_1_out, nor_6_out, nor_9_out);
  nor nor_8 (nor_8_out, and_20_out, and_19_out, and_23_out, and_25_out);
  and and_24 (and_24_out, a2, S3, b2);
  nor nor_9 (nor_9_out, and_22_out, and_24_out);
  and and_25 (and_25_out, m, c0, nor_3_out, nor_6_out, nor_9_out);
  and and_26 (and_26_out, ~nor_10_out, nor_11_out);  // AND_Gate
  xor xor_4 (f3, nor_8_out, and_26_out);
  and and_27 (and_27_out, b3, S0);
  and and_28 (and_28_out, S1, ~b3);  // AND_Gate
  nor nor_10 (nor_10_out, a3, and_27_out, and_28_out);
  nand nand_2 (p, nor_3_out, nor_6_out, nor_9_out, nor_11_out);
  nand nand_3 (nand_3_out, c0, nor_3_out, nor_6_out, nor_9_out, nor_11_out);
  or or_1 (c4, ~nand_3_out, ~g);  // OR_Gate
  and and_29 (and_29_out, a3, S3, b3);
  and and_30 (and_30_out, ~b3, S2, a3);  // AND_Gate
  nor nor_11 (nor_11_out, and_30_out, and_29_out);
  and and_31 (and_31_out, nor_1_out, nor_6_out, nor_9_out, nor_11_out);
  and and_32 (and_32_out, nor_7_out, nor_11_out);
  and and_33 (and_33_out, nor_4_out, nor_9_out, nor_11_out);
  nor nor_12 (g, and_31_out, and_33_out, and_32_out, nor_10_out);
endmodule
